# Fritzing sketch jinglebells_spiezo (saved by Fritzing 0.9.3b)
breadboards: 1

parts:
  J1 = Piezo Speaker
  Netduino1 = Netduino Plus2

nets:
  N1: J1.pin1, Netduino1.GND
  N2: J1.pin2, Netduino1.D5_PWM0
